# Fritzing sketch pi-display-connections (saved by Fritzing 0.9.9b)

parts:
  MCU1 = Raspberry Pi Zero
  J1 = shrouded pin header, 16 pins [form="♂ (shrouded male)"]
  J2 = shrouded pin header, 16 pins [form="♂ (shrouded male)"]

nets:
  N1: MCU1.pin_1, MCU1.pin_17, J1.pin16, J2.pin16
  N2: MCU1.pin_6, MCU1.pin_25, J1.pin1, J2.pin1
  N3: MCU1.pin_12, J2.pin9
  N4: MCU1.pin_18, J1.pin10
  N5: MCU1.pin_19, J1.pin3
  N6: MCU1.pin_22, J1.pin8
  N7: MCU1.pin_23, J1.pin15
  N8: MCU1.pin_24, J1.pin9
  N9: MCU1.pin_29, J2.pin10
  N10: MCU1.pin_31, J2.pin8
  N11: MCU1.pin_38, J2.pin3
  N12: MCU1.pin_40, J2.pin15

notes:
  OLED pins as viewed from back of PCB with connector on left
  Display 1
  Display 2
